// Logisim project 6.circ as structural Verilog: 1 circuit, main circuit multiplexor
module multiplexor (
  input  [2:0] inputzero,
  input  [2:0] inputone,
  input  [2:0] inputtwo,
  input  [2:0] inputthree,
  input  [1:0] selector,
  output [2:0] muxoutput
);
endmodule
