// Logisim project extracredit.circ as structural Verilog: 1 circuit, main circuit tripledigit
module tripledigit (
  input  [9:0] thousand,
  output [6:0] hundreds,
  output [6:0] tens,
  output [6:0] ones
);
endmodule
