// Logisim project lab1problem1.circ as structural Verilog: 1 circuit, main circuit introduction
module introduction (
  input  A,
  input  B,
  input  C,
  input  D,
  output f,
  output g
);
endmodule
