// Logisim project lab1problem5.circ as structural Verilog: 1 circuit, main circuit singledigit
module singledigit (
  input  [3:0] i,
  output a,
  output b,
  output c,
  output d,
  output e,
  output f,
  output g
);
endmodule
