// Logisim project 6.circ as structural Verilog: 1 circuit, main circuit cla
module cla (
  input  [3:0] inputa,
  input  [3:0] inputb,
  input  carryin,
  output [3:0] carryout,
  output [3:0] generator,
  output [3:0] propagator
);
endmodule
