// Logisim project 7.circ as structural Verilog: 1 circuit, main circuit alu
module alu (
  input  [3:0] inputa,
  input  [3:0] inputb,
  input  [2:0] operation,
  output [3:0] aluout
);
endmodule
