// Logisim project 2.circ as structural Verilog: 1 circuit, main circuit tregister
module tregister (
  input  [7:0] eightbitinput,
  input  sysclock,
  output [7:0] registerval
);
endmodule
