// Logisim project 7.circ as structural Verilog: 1 circuit, main circuit vendingmachine
module vendingmachine (
  input  input5,
  input  input10,
  input  input20,
  input  sysclock,
  output outputcoke,
  output output5,
  output output10
);
endmodule
