// Logisim project 4.circ as structural Verilog: 1 circuit, main circuit cpu
module cpu (
  input  resetall,
  input  sysclock,
  output [7:0] pc,
  output [7:0] x0,
  output [7:0] x1,
  output [7:0] x2,
  output [7:0] x3,
  output [7:0] x4,
  output [7:0] x5,
  output [7:0] x6,
  output [7:0] x7
);
endmodule
