// Logisim project extracredit.circ as structural Verilog: 1 circuit, main circuit ledger
module ledger (
  input  [2:0] customerid,
  input  [1:0] transactiontype,
  input  [7:0] transactionamount,
  input  sysclock,
  output [1:0] transactionresult,
  output [7:0] amountremaining
);
endmodule
